// Digital circuit Assembly Workspace.dig as structural Verilog
module Assembly_Workspace (
  input  clk
);

  wire button_1_out, button_2_out, telescope_assembler_computer_1_p6, telescope_assembler_computer_1_p9,
       telescope_assembler_computer_1_p13, telescope_assembler_computer_1_p14,
       telescope_assembler_computer_1_p15, telescope_assembler_computer_1_p16,
       telescope_assembler_computer_1_p17, telescope_assembler_computer_1_p18,
       telescope_assembler_computer_1_p19, telescope_assembler_computer_1_p20, undriven;
  wire [6:0] Text_Input_d;
  wire [15:0] telescope_assembler_computer_1_p3, telescope_assembler_computer_1_p7,
       telescope_assembler_computer_1_p8, telescope_assembler_computer_1_p11,
       telescope_assembler_computer_1_p12;
  wire [31:0] telescope_assembler_computer_1_p10;

  ROM #(.AddrBits(24), .Bits(7)) Text_Input (
    .A(telescope_assembler_computer_1_p10[23:0]), .sel(1'b1), .D(Text_Input_d));
  Button button_1 (.out(button_1_out));
  Button button_2 (.out(button_2_out));
  // Telescope_Assembler_Computer telescope_assembler_computer_1: pin names not known; wires that end beside it: button_1_out, clk, telescope_assembler_computer_1_p3, Text_Input_d, button_2_out, telescope_assembler_computer_1_p6, telescope_assembler_computer_1_p7, telescope_assembler_computer_1_p8, telescope_assembler_computer_1_p9, telescope_assembler_computer_1_p10, telescope_assembler_computer_1_p11, telescope_assembler_computer_1_p12, telescope_assembler_computer_1_p13, telescope_assembler_computer_1_p14, telescope_assembler_computer_1_p15, telescope_assembler_computer_1_p16, telescope_assembler_computer_1_p17, telescope_assembler_computer_1_p18, telescope_assembler_computer_1_p19, telescope_assembler_computer_1_p20
  RAMDualPort #(.AddrBits(16), .isProgramMemory("true"), .Bits(16)) Assembler_MC (
    .A(telescope_assembler_computer_1_p7), .Din(telescope_assembler_computer_1_p8),
    .str(telescope_assembler_computer_1_p9), .C(clk), .ld(1'b1), .D(telescope_assembler_computer_1_p3));
  LED led_1 (.in(telescope_assembler_computer_1_p16));
  LED led_2 (.in(telescope_assembler_computer_1_p17));
  LED led_3 (.in(telescope_assembler_computer_1_p18));
  LED led_4 (.in(telescope_assembler_computer_1_p19));
  LED led_5 (.in(telescope_assembler_computer_1_p20));
  LED led_6 (.in(undriven));
  // Probe Cycles Used on telescope_assembler_computer_1_p6
  EEPROMDualPort #(.AddrBits(16), .Bits(16)) MC_Output (
    .A(telescope_assembler_computer_1_p11), .Din(telescope_assembler_computer_1_p12),
    .str(telescope_assembler_computer_1_p13), .C(clk), .ld(1'b0));  // open: D
  Terminal #(.termWidth(130), .termHeight(40)) File_As_Read (
    .D(telescope_assembler_computer_1_p14), .C(clk), .en(telescope_assembler_computer_1_p15));

  // Notes on the sheet:
  //   clk: Hz: 2147483647
  //   contents of Text_Input (hex, n*v repeats v):
  //   4a,4d,50,20,3e,53,74,61,72,74,50,6f,69,6e,74,a,a,28,2f,20,43,6f
  //   ,6e,73,74,61,6e,74,73,2c,20,76,61,72,69,61,62,6c,65,73,2c,20,61
  //   ,6e,64,20,74,61,62,6c,65,73,2e,a,40,49,4e,46,4c,47,20,3d,20,30
  //   ,a,40,4f,55,54,46,4c,47,20,3d,20,30,78,38,30,30,a,a,40,54,41,42
  //   ,4c,45,53,54,4f,50,20,3d,20,30,78,4*46,20,20,2f,20,4d,75,73,74
  //   ,20,73,74,61,79,20,4e,55,4c,4c,2e,a,a,40,43,41,4c,48,41,53,48
  //   ,20,3d,20,30,78,62,30,32,33,a,a,2f,20,49,6e,73,74,72,75,63,74
  //   ,69,6f,6e,20,74,61,62,6c,65,20,65,6e,74,72,69,65,73,3a,20,28,6d
  //   ,6e,65,6d,6f,6e,69,63,5f,68,61,73,68,2c,20,74,72,61,6e,73,6c,61
  //   ,74,69,6f,6e,2c,20,6f,70,65,72,61,6e,64,5f,62,69,74,6d,61,70,29
  //   ,a,23,49,6e,73,74,54,61,62,6c,65,20,3d,20,28,30,78,64,39,65,64
  //   ,2c,20,30,78,33,30,30,30,2c,20,30,62,30,30,31,31,2c,20,20,2f,20
  //   ,4d,4f,56,a,14*20,30,78,39,39,32,61,2c,20,30,78,34,30,30,30,2c
  //   ,20,30,62,30,31,30,30,2c,20,20,2f,20,4a,49,46,a,14*20,30,78,61
  //   ,34,38,63,2c,20,30,78,35,30,30,30,2c,20,30,62,30,30,31,30,2c,20,20
  //   ,2f,20,4c,44,49,a,14*20,30,78,39,31,65,63,2c,20,30,78,36,30,30,30
  //   ,2c,20,30,62,30,30,31,31,2c,20,20,2f,20,4c,4f,44,a,14*20,30,78
  //   ,63,61,39,33,2c,20,30,78,37,30,30,30,2c,20,30,62,30,30,31,31,2c
  //   ,20,20,2f,20,53,54,52,a,14*20,30,78,39,39,38,31,2c,20,30,78,38
  //   ,30,30,30,2c,20,30,62,30,31,31,31,2c,20,20,2f,20,41,4c,46,a,14*20
  //   ,30,78,39,39,32,31,2c,20,30,78,39,30,30,30,2c,20,30,62,4*31,2c
  //   ,20,20,2f,20,41,49,46,a,14*20,30,78,64,35,38,31,2c,20,30,78,41
  //   ,30,30,30,2c,20,30,62,30,31,31,31,2c,20,20,2f,20,41,4c,55,a,14*20
  //   ,30,78,61,35,38,31,2c,20,30,78,42,30,30,30,2c,20,30,62,4*31,2c
  //   ,20,20,2f,20,41,4c,49,a,14*20,30,78,62,38,63,31,2c,20,30,78,43
  //   ,30,30,30,2c,20,30,62,30,31,31,31,2c,20,20,2f,20,41,46,4e,a,14*20
  //   ,30,78,62,39,32,31,2c,20,30,78,44,30,30,30,2c,20,30,62,4*31,2c
  //   ,20,20,2f,20,41,49,4e,a,9,9,9,20,20,30,78,64,30,62,32,2c,20,30
  //   ,78,33,30,38,37,2c,20,30,62,4*30,2c,20,20,2f,20,52,45,54,a,14*20
  //   ,30,78,62,65,35,61,2c,20,30,78,62,31,30,30,2c,20,30,62,30,30,31
  //   ,30,2c,20,20,2f,20,5a,52,4f,a,14*20,30,78,62,32,61,65,2c,20,30
  //   ,78,62,30,30,30,2c,20,30,62,30,30,31,30,2c,20,20,2f,20,4e,55,4c
  //   ,a,14*20,30,78,63,63,33,30,2c,20,30,78,39,32,30,30,2c,20,30,62
  //   ,30,30,31,30,2c,20,20,2f,20,50,41,53,a,14*20,30,78,61,32,37,30
  //   ,2c,20,30,78,62,62,62,30,2c,20,30,62,31,30,30,31,2c,20,20,2f,20
  //   ,50,53,48,a,14*20,30,78,63,31,66,30,2c,20,30,78,62,39,62,30,2c
  //   ,20,30,62,31,30,30,31,2c,20,20,2f,20,50,4f,50,a,14*20,30,78,63
  //   ,31,61,33,2c,20,30,78,63,62,30,30,2c,20,30,62,30,30,31,31,2c,20,20
  //   ,2f,20,43,4d,50,a,14*20,30,78,63,31,61,61,2c,20,30,78,34,36,30,30
  //   ,2c,20,30,62,4*30,2c,20,20,2f,20,4a,4d,50,a,14*20,30,78,63,34
  //   ,61,61,2c,20,30,78,34,30,30,30,2c,20,30,62,4*30,2c,20,20,2f,20
  //   ,4a,45,51,a,14*20,30,78,39,35,63,61,2c,20,30,78,34,38,30,30,2c
  //   ,20,30,62,4*30,2c,20,20,2f,20,4a,4e,45,a,14*20,30,78,64,31,38
  //   ,61,2c,20,30,78,34,31,30,30,2c,20,30,62,4*30,2c,20,20,2f,20,4a
  //   ,4c,54,a,14*20,30,78,39,34,65,61,2c,20,30,78,34,39,30,30,2c,20
  //   ,30,62,4*30,2c,20,20,2f,20,4a,47,45,a,9,9,9,20,20,30,78,63,66
  //   ,33,33,2c,20,30,78,32,30,30,30,2c,20,30,62,4*30,2c,20,20,2f,20
  //   ,53,59,53,a,9,9,9,20,20,30,78,62,36,37,32,2c,20,30,78,31,30,30,30
  //   ,2c,20,30,62,4*30,2c,20,20,2f,20,52,53,4d,a,9,9,9,20,20,30,78
  //   ,64,31,38,38,2c,20,30,78,4*30,2c,20,30,62,4*30,2c,20,20,2f,20
  //   ,48,4c,54,a,9,9,9,20,20,30,78,63,31,65,65,2c,20,30,78,46,30,30,30
  //   ,2c,20,30,62,4*30,2c,20,20,2f,20,4e,4f,50,a,14*20,3e,54,41,42
  //   ,4c,45,53,54,4f,50,a,14*20,29,a,a,2f,20,52,65,67,69,73,74,65,72
  //   ,20,74,61,62,6c,65,20,65,6e,74,72,69,65,73,3a,20,28,6d,6e,65,6d
  //   ,6f,6e,69,63,5f,68,61,73,68,2c,20,74,72,61,6e,73,6c,61,74,69,6f
  //   ,6e,29,a,23,52,65,67,54,61,62,6c,65,20,3d,20,28,30,78,34,30,46
  //   ,32,2c,20,30,78,30,2c,20,20,2f,20,52,47,30,a,9,9,9,20,30,78,34,34
  //   ,46,32,2c,20,30,78,31,2c,20,20,2f,20,52,47,31,a,9,9,9,20,30,78
  //   ,34,38,46,32,2c,20,30,78,32,2c,20,20,2f,20,52,47,32,a,9,9,5*20
  //   ,30,78,34,43,46,32,2c,20,30,78,33,2c,20,20,2f,20,52,47,33,a,9,9
  //   ,5*20,30,78,35,30,46,32,2c,20,30,78,34,2c,20,20,2f,20,52,47,34
  //   ,a,9,9,5*20,30,78,35,34,46,32,2c,20,30,78,35,2c,20,20,2f,20,52
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  //   Make sure output is cleared (and make sure to press OK)
endmodule
