// Digital circuit Telescope Assembler Computer.dig as structural Verilog
module Telescope_Assembler_Computer (
  input  Start,
  input  Clock,
  input  [15:0] RAM_Input,
  input  [6:0] Text_Input,
  input  Pause,
  output [31:0] Cycles_Used,
  output [15:0] RTL_File_Line,
  output [15:0] RAM_Address,
  output [15:0] RAM_Output,
  output RAM_Write,
  output [31:0] Text_Address,
  output [15:0] Output_Address,
  output [15:0] Output_Data,
  output Output_Write,
  output [6:0] Terminal_Data,
  output Terminal_Write,
  output Bad_Number,
  output Label_Not_Found,
  output Non_Empty_Stack,
  output Instruction_Not_Found,
  output Operand_Not_Found,
  output Success
);

  wire demultiplexer_2_out_0, glass_cpu_1_clock_out, glass_cpu_1_is_running, glass_cpu_1_writing_i_o;
  wire [4:0] glass_cpu_1_iop;
  wire [15:0] driverinvsel_1_out, glass_cpu_1_i_o_out, glass_cpu_1_pc;

  assign driverinvsel_1_out = ~glass_cpu_1_is_running ? RAM_Input : 16'bz;  // DriverInvSel driverinvsel_1
  PullDown #(.Bits(16)) pulldown_1 (.out(driverinvsel_1_out));
  Glass_CPU glass_cpu_1 (
    .Start(Start), .Pause(Pause), .Clock_In(Clock), .RAM_Input(RAM_Input), .I_O_In({{9{1'b0}}, Text_Input}),
    .I_O_Reading(1'b0), .I_O_Writing(1'b0), .Int_Lines(4'b0000), .Interrupt_Mask(4'b0000), .Hard_Reset(1'b0),
    .RAM_Addr(RAM_Address), .RAM_Output(RAM_Output), .RAM_Write(RAM_Write), .PC(glass_cpu_1_pc),
    .IOP(glass_cpu_1_iop), .Clock_Out(glass_cpu_1_clock_out), .Is_Running(glass_cpu_1_is_running),
    .Reading_I_O(Terminal_Write), .I_O_Out(glass_cpu_1_i_o_out), .Writing_I_O(glass_cpu_1_writing_i_o));  // open: HLB, Is_Kernel
  Demultiplexer #(.Bits(16)) demultiplexer_1 (
    .sel(glass_cpu_1_iop[0]), .in(glass_cpu_1_i_o_out), .out_1(Output_Data));  // open: out_0
  PullDown #(.Bits(16)) pulldown_2 (.out(glass_cpu_1_i_o_out));
  Demultiplexer demultiplexer_2 (
    .sel(glass_cpu_1_iop[0]), .in(glass_cpu_1_writing_i_o), .out_0(demultiplexer_2_out_0),
    .out_1(Output_Write));
  Add #(.Bits(16)) add_1 (.a(glass_cpu_1_pc), .b(16'h2), .c_i(1'b0), .s(RTL_File_Line));  // open: c_o
  Counter #(.Bits(32)) counter_1 (.en(1'b1), .C(glass_cpu_1_clock_out), .clr(1'b0), .out(Cycles_Used));  // open: ovf
  Counter #(.Bits(32)) counter_2 (
    .en(Terminal_Write), .C(Clock), .clr(demultiplexer_2_out_0), .out(Text_Address));  // open: ovf
  Counter #(.Bits(16)) counter_3 (.en(Output_Write), .C(Clock), .clr(1'b0), .out(Output_Address));  // open: ovf
  Comparator #(.Bits(16)) comparator_1 (.a(driverinvsel_1_out), .b(16'hfff0), .eq(Bad_Number));  // open: gt, lt
  Comparator #(.Bits(16)) comparator_2 (.a(driverinvsel_1_out), .b(16'hfff1), .eq(Label_Not_Found));  // open: gt, lt
  Comparator #(.Bits(16)) comparator_3 (.a(driverinvsel_1_out), .b(16'hfff2), .eq(Non_Empty_Stack));  // open: gt, lt
  Comparator #(.Bits(16)) comparator_4 (
    .a(driverinvsel_1_out), .b(16'hfff3), .eq(Instruction_Not_Found));  // open: gt, lt
  Comparator #(.Bits(16)) comparator_5 (.a(driverinvsel_1_out), .b(16'hfff4), .eq(Operand_Not_Found));  // open: gt, lt
  Comparator #(.Bits(16)) comparator_6 (.a(driverinvsel_1_out), .b(16'h1), .eq(Success));  // open: gt, lt

  assign Terminal_Data = Text_Input;
endmodule
