// Digital circuit Telescope Testspace.dig as structural Verilog
module Telescope_Testspace (
);

  // Telescope_Computing_System telescope_computing_system_1: pin names not known; wires that end beside it: {19{1'b0}}, {18{1'b0}}, {18{1'b0}}
endmodule
