// Digital circuit Test Sandbox.dig as structural Verilog
module Test_Sandbox (
  input  clk
);

  wire button_1_out, button_2_out, glass_cpu_1_p13, glass_cpu_1_p15, glass_cpu_1_p16, glass_cpu_1_p17,
       glass_cpu_1_p18, glass_cpu_1_p20;
  wire [3:0] counter_1_out, counter_3_out;
  wire [15:0] add_1_s, glass_cpu_1_p4, glass_cpu_1_p11, glass_cpu_1_p12, glass_cpu_1_p14, glass_cpu_1_p19,
       rom_1_d;
  wire [31:0] counter_2_out;

  Counter #(.Bits(4)) counter_1 (.en(glass_cpu_1_p18), .C(clk), .clr(1'b0), .out(counter_1_out));  // open: ovf
  ROM #(.AddrBits(4), .Bits(16)) rom_1 (.A(counter_1_out), .sel(1'b1), .D(rom_1_d));
  Button button_1 (.out(button_1_out));
  Button button_2 (.out(button_2_out));
  // Glass_CPU glass_cpu_1: pin names not known; wires that end beside it: button_1_out, button_2_out, clk, glass_cpu_1_p4, rom_1_d, 1'b1, 1'b1, 3'b000, 1'b0, 1'b0, glass_cpu_1_p11, glass_cpu_1_p12, glass_cpu_1_p13, glass_cpu_1_p14, glass_cpu_1_p15, glass_cpu_1_p16, glass_cpu_1_p17, glass_cpu_1_p18, glass_cpu_1_p19, glass_cpu_1_p20
  LED led_1 (.in(glass_cpu_1_p17));
  Counter #(.Bits(32)) counter_2 (.en(1'b1), .C(glass_cpu_1_p16), .clr(1'b0), .out(counter_2_out));  // open: ovf
  Add #(.Bits(16)) add_1 (.a(glass_cpu_1_p14), .b(16'h2), .c_i(1'b0), .s(add_1_s));  // open: c_o
  RAMDualPort #(.AddrBits(16), .isProgramMemory("true"), .Bits(16)) Program_Memory (
    .A(glass_cpu_1_p11), .Din(glass_cpu_1_p12), .str(glass_cpu_1_p13), .C(clk), .ld(1'b1), .D(glass_cpu_1_p4));
  Counter #(.Bits(4)) counter_3 (.en(glass_cpu_1_p20), .C(clk), .clr(1'b0), .out(counter_3_out));  // open: ovf
  // Probe Memory Address on glass_cpu_1_p11
  // Probe Cycles Used on counter_2_out
  // Probe RTL Line on add_1_s
  // Probe Test IOP on glass_cpu_1_p15
  RAMDualPort #(.AddrBits(4), .Bits(16)) ramdualport_1 (
    .A(counter_3_out), .Din(glass_cpu_1_p19), .str(glass_cpu_1_p20), .C(clk), .ld(1'b0));  // open: D

  // Notes on the sheet:
  //   clk: Hz: 32
  //   contents of rom_1 (hex, n*v repeats v):
  //   5,4,3,8,1,2,6,9,7,0,a
endmodule
