// Digital circuit Assembly Workspace.dig as structural Verilog
module Assembly_Workspace (
  input  clk,
  output [15:0] Code
);

  wire button_1_out, telescope_assembler_computer_1_p4, telescope_assembler_computer_1_p8,
       telescope_assembler_computer_1_p9, telescope_assembler_computer_1_p10;
  wire [6:0] Text_Input_d;
  wire [15:0] telescope_assembler_computer_1_p6, telescope_assembler_computer_1_p7;
  wire [23:0] telescope_assembler_computer_1_p5;

  ROM #(.AddrBits(24), .Bits(7)) Text_Input (.A(telescope_assembler_computer_1_p5), .sel(1'b1), .D(Text_Input_d));
  Button button_1 (.out(button_1_out));
  // Telescope_Assembler_Computer telescope_assembler_computer_1: pin names not known; wires that end beside it: button_1_out, clk, Text_Input_d, telescope_assembler_computer_1_p4, telescope_assembler_computer_1_p5, telescope_assembler_computer_1_p6, telescope_assembler_computer_1_p7, telescope_assembler_computer_1_p8, telescope_assembler_computer_1_p9, telescope_assembler_computer_1_p10, Code
  LED led_1 (.in(telescope_assembler_computer_1_p4));
  EEPROMDualPort #(.AddrBits(16), .Bits(16)) MC_Output (
    .A(telescope_assembler_computer_1_p6), .Din(telescope_assembler_computer_1_p7),
    .str(telescope_assembler_computer_1_p8), .C(clk), .ld(1'b0));  // open: D
  Terminal #(.termWidth(130), .termHeight(40)) terminal_1 (
    .D(telescope_assembler_computer_1_p9), .C(clk), .en(telescope_assembler_computer_1_p10));

  // Notes on the sheet:
  //   clk: Hz: 2147483647
  //   Make sure MC Output is cleared (and make sure to press OK)
endmodule
