// Digital circuit Bootloader Machine.dig as structural Verilog
module Bootloader_Machine (
  input  Boot_Start,
  input  Pause,
  input  Clock_In,
  input  [15:0] Load_Din,
  input  [15:0] I_O_In,
  input  I_O_Reading,
  input  I_O_Writing,
  input  [3:0] Int_Lines,
  input  [3:0] Int_Mask,
  input  Hard_Reset,
  output Running,
  output [15:0] Load_Adr,
  output [15:0] PC,
  output [15:0] HLB,
  output Kernel,
  output Reading_I_O,
  output [15:0] I_O_Out,
  output Writing_I_O,
  output [4:0] IOP,
  output LO_Enabled
);

  wire and_1_out, and_2_out, and_3_out, and_4_out, Boot_Counter_ovf, Booting_q, delay_1_out, delay_2_out,
       Done_Booting_q, glass_cpu_1_ram_str, or_1_out, or_2_out, or_3_out, or_4_out, rs_ff_as_1_nq,
       rs_ff_as_1_q, Starting_q;
  wire [15:0] add_1_s, Boot_Counter_out, Boot_PC_out, glass_cpu_1_ram_a, glass_cpu_1_ram_dout,
       multiplexer_1_out, multiplexer_2_out, multiplexer_3_out, sub_1_s, Working_Memory__RAM_d;

  Delay delay_1 (.in(Boot_Start), .out(delay_1_out));
  and and_1 (and_1_out, Boot_Start, ~or_1_out, ~delay_1_out);  // And
  or or_1 (or_1_out, or_3_out, Done_Booting_q);
  RS_FF_AS rs_ff_as_1 (.S(and_1_out), .R(or_3_out), .Q(rs_ff_as_1_q), .nQ(rs_ff_as_1_nq));
  and and_2 (and_2_out, Boot_Start, Done_Booting_q);
  and and_3 (and_3_out, Pause, Done_Booting_q);
  RS_FF Done_Booting (.S(Boot_Counter_ovf), .C(~Clock_In), .R(Hard_Reset), .Q(Done_Booting_q));  // open: nQ
  Delay delay_2 (.in(Done_Booting_q), .out(delay_2_out));
  RS_FF Starting (.S(rs_ff_as_1_q), .C(~Clock_In), .R(rs_ff_as_1_nq), .Q(Starting_q));  // open: nQ
  or or_2 (or_2_out, and_4_out, and_2_out);
  and and_4 (and_4_out, Done_Booting_q, ~delay_2_out);  // And
  Glass_CPU glass_cpu_1 (
    .Start(or_2_out), .Pause(and_3_out), .Clock_In(Clock_In), .RAM_Din(Working_Memory__RAM_d),
    .I_O_In(I_O_In), .I_O_Reading(I_O_Reading), .I_O_Writing(I_O_Writing), .Int_Lines(Int_Lines),
    .Int_Mask(Int_Mask), .Hard_Reset(Hard_Reset), .Running(Running), .RAM_A(glass_cpu_1_ram_a),
    .RAM_Dout(glass_cpu_1_ram_dout), .RAM_Str(glass_cpu_1_ram_str), .PC(PC), .HLB(HLB), .Kernel(Kernel),
    .Reading_I_O(Reading_I_O), .I_O_Out(I_O_Out), .Writing_I_O(Writing_I_O), .IOP(IOP),
    .LO_Enabled(LO_Enabled));
  RS_FF Booting (.S(Starting_q), .C(~Clock_In), .R(Boot_Counter_ovf), .Q(Booting_q));  // open: nQ
  or or_3 (or_3_out, Starting_q, Booting_q);
  Counter #(.Bits(16)) Boot_PC (.en(Booting_q), .C(Clock_In), .clr(Hard_Reset), .out(Boot_PC_out));  // open: ovf
  CounterPreset #(.Bits(16)) Boot_Counter (
    .en(Booting_q), .C(Clock_In), .dir(1'b1), .in(Load_Din), .ld(Starting_q), .clr(1'b0),
    .out(Boot_Counter_out), .ovf(Boot_Counter_ovf));
  // Probe on Boot_Counter_out
  Multiplexer #(.Bits(16)) multiplexer_1 (
    .sel(Booting_q), .in_0(glass_cpu_1_ram_a), .in_1(Boot_PC_out), .out(multiplexer_1_out));
  Multiplexer #(.Bits(16)) multiplexer_2 (
    .sel(Booting_q), .in_0(glass_cpu_1_ram_dout), .in_1(Load_Din), .out(multiplexer_2_out));
  or or_4 (or_4_out, Booting_q, glass_cpu_1_ram_str);
  Add #(.Bits(16)) add_1 (.a(multiplexer_1_out), .b(16'h2), .c_i(1'b0), .s(add_1_s));  // open: c_o
  Sub #(.Bits(16)) sub_1 (.a(add_1_s), .b({HLB[7:0], {8{1'b0}}}), .c_i(1'b0), .s(sub_1_s));  // open: c_o
  // Probe RAM Adr Dec on multiplexer_1_out
  // Probe RAM Adr Hex on multiplexer_1_out
  RAMDualPort #(.AddrBits(16), .Bits(16)) Working_Memory__RAM (
    .A(multiplexer_1_out), .Din(multiplexer_2_out), .str(or_4_out), .C(Clock_In), .ld(1'b1),
    .D(Working_Memory__RAM_d));
  Counter #(.Bits(16)) Load_PC (.en(or_3_out), .C(Clock_In), .clr(1'b0), .out(Load_Adr));  // open: ovf
  Multiplexer #(.Bits(16)) multiplexer_3 (.sel(LO_Enabled), .in_0(add_1_s), .in_1(sub_1_s), .out(multiplexer_3_out));
  // Probe RAM Output on Working_Memory__RAM_d
  // Probe Lo Enabled on LO_Enabled
  // Probe RTL Line on multiplexer_3_out

  // Notes on the sheet:
  //   Boot_Start: Starts/Resumes the execution of program memory.
  //   Only starts/resumes on rising edge (so if Start is held high the CPU can still halt)
  //   Pause: Pauses the execution of program memory.
  //   Only pauses on rising edge.
  //   Load_Din: The boot drive data input
  //   I_O_In: The Input portion of I/O
  //   I_O_Reading: Should be high if the I/O wants to read from the CPU.
  //   Is a jump condition (PIR/PNR)
  //   I_O_Writing: Should be high if the I/O wants to write to the CPU.
  //   Is a jump condition (PIW/PNW).
  //   Int_Mask: Each bit corresponds to one interrupt line.
  //   If the bit is on, then that interrupt is non-maskable.
  //   Hard_Reset: Effectively resets the CPU.
  //   Only clears the state counter, PC, and parts of FLG.
  //   It must be held down for at least 2 full clock cycles to work.
  //   Running: Only on if the CPU is currently executing program memory.
  //   Load_Adr: Address output for the boot drive
  //   PC: The current value of the program counter.
  //   HLB: The contents of the HI/LO Bounds register.
  //   Kernel: On if the current process is kernel.
  //   I/O devices can choose whether they respond to non-kernel processes.
  //   Reading_I_O: On if the CPU is currently reading from Input.
  //   I_O_Out: The Output portion of I/O
  //   Writing_I_O: On if the CPU is currently writing to output.
  //   IOP: The currently selected I/O device.
  //   Note: I/O must be multiplexed according to this signal *outside* the CPU.
  //   LO_Enabled: LO offsetting is currently enabled.
endmodule
