// Digital circuit Telescope Computing System.dig as structural Verilog
module Telescope_Computing_System (
  input  Power_On,
  input  [15:0] OS_In,
  input  STOP,
  input  Clock_Input,
  input  [15:0] D0_In,
  input  [15:0] D1_In,
  input  [15:0] D2_In,
  input  [15:0] D3_In,
  input  Pause_CPU,
  input  [17:0] GPI_0,
  input  [17:0] GPI_1,
  input  [17:0] GPI_2,
  input  [17:0] GPI_3,
  input  [19:0] TNET_I_0,
  input  PAUS,
  input  [16:0] K0_In,
  input  [16:0] K1_In,
  input  [16:0] K2_In,
  input  [16:0] K3_In,
  input  [19:0] TNET_I_1,
  input  [19:0] TNET_I_2,
  input  [19:0] TNET_I_3,
  output [15:0] OS_Adr,
  output Running,
  output [33:0] D0_Out,
  output [33:0] D1_Out,
  output [33:0] D2_Out,
  output [33:0] D3_Out,
  output [18:0] GPO_0,
  output [18:0] GPO_1,
  output [18:0] GPO_2,
  output [18:0] GPO_3,
  output [19:0] TNET_O_0,
  output [15:0] Status_Code,
  output [18:0] TK0_Out,
  output [18:0] TK1_Out,
  output [18:0] TK2_Out,
  output [18:0] TK3_Out,
  output [19:0] TNET_O_1,
  output [19:0] TNET_O_2,
  output [19:0] TNET_O_3
);

  wire and_1_out, and_2_out, and_3_out, and_4_out, and_6_out, and_7_out, bootloader_machine_1_kernel,
       delay_1_out, delay_2_out, delay_3_out, delay_4_out, nor_1_out, or_1_out, or_2_out, or_3_out, or_4_out,
       or_5_out, or_6_out, or_7_out, rs_ff_2_nq, rs_ff_as_1_q, rs_ff_as_2_q, rs_ff_as_3_q, rs_ff_as_5_q;
  wire [0:0] demultiplexer_1_out_0, demultiplexer_1_out_1, demultiplexer_1_out_2, demultiplexer_1_out_3;
  wire [1:0] bootloader_machine_1_writing_i_o, demultiplexer_1_out_4, demultiplexer_1_out_5,
       demultiplexer_1_out_6, demultiplexer_1_out_7, demultiplexer_1_out_16, demultiplexer_1_out_17,
       demultiplexer_1_out_18, demultiplexer_1_out_19, demultiplexer_1_out_28, demultiplexer_1_out_29,
       demultiplexer_1_out_30, demultiplexer_1_out_31, driver_10_out;
  wire [3:0] rs_ff_1_q;
  wire [3:3] bootloader_machine_1_lo_enabled;
  wire [4:0] bootloader_machine_1_iop;
  wire [15:0] bootloader_machine_1_i_o_out, RNG_r;
  wire [17:0] multiplexer_1_out, pulldown_1_out, tnet_1_pc_do, tnet_2_pc_do, tnet_3_pc_do, tnet_4_pc_do;
  wire [31:0] counter_1_out;

  assign TK0_Out[15:0] = TK0_Out[17] ? bootloader_machine_1_i_o_out : 16'bz;  // Driver driver_1
  assign TK1_Out[15:0] = TK1_Out[17] ? bootloader_machine_1_i_o_out : 16'bz;  // Driver driver_2
  assign TK2_Out[15:0] = TK2_Out[17] ? bootloader_machine_1_i_o_out : 16'bz;  // Driver driver_3
  assign TK3_Out[15:0] = TK3_Out[17] ? bootloader_machine_1_i_o_out : 16'bz;  // Driver driver_4
  Delay delay_1 (.in(bootloader_machine_1_lo_enabled[3]), .out(delay_1_out));
  and and_1 (and_1_out, delay_1_out, ~bootloader_machine_1_lo_enabled[3]);  // And
  Delay delay_2 (.in(counter_1_out[14]), .out(delay_2_out));
  RS_FF_AS rs_ff_as_1 (.S(and_1_out), .R(rs_ff_2_nq), .Q(rs_ff_as_1_q));  // open: nQ
  assign GPO_0[15:0] = GPO_0[17] ? bootloader_machine_1_i_o_out : 16'bz;  // Driver driver_5
  and and_2 (and_2_out, counter_1_out[14], ~delay_2_out);  // And
  RS_FF_AS rs_ff_as_2 (.S(PAUS), .R(rs_ff_1_q[1]), .Q(rs_ff_as_2_q));  // open: nQ
  RS_FF_AS rs_ff_as_3 (.S(STOP), .R(rs_ff_1_q[3]), .Q(rs_ff_as_3_q));  // open: nQ
  RS_FF_AS rs_ff_as_4 (.S(and_2_out), .R(demultiplexer_1_out_31[1]), .Q(rs_ff_1_q[0]));  // open: nQ
  RS_FF rs_ff_1 (.S(rs_ff_as_2_q), .C(Clock_Input), .R(rs_ff_as_1_q), .Q(rs_ff_1_q[1]));  // open: nQ
  RS_FF rs_ff_2 (.S(rs_ff_as_3_q), .C(Clock_Input), .R(rs_ff_as_1_q), .Q(rs_ff_1_q[3]), .nQ(rs_ff_2_nq));
  assign GPO_1[15:0] = GPO_1[17] ? bootloader_machine_1_i_o_out : 16'bz;  // Driver driver_6
  Multiplexer #(.Selector_Bits(5), .Bits(18)) multiplexer_1 (
    .sel(bootloader_machine_1_iop), .in_0({2'b11, D0_In}), .in_1({2'b11, D1_In}), .in_2({2'b11, D2_In}),
    .in_3({2'b11, D3_In}), .in_4({2'b11, D0_Out[15:0]}), .in_5({2'b11, D1_Out[15:0]}),
    .in_6({2'b11, D2_Out[15:0]}), .in_7({2'b11, D3_Out[15:0]}), .in_8({K0_In[16], 1'b1, K0_In[15:0]}),
    .in_9({K1_In[16], 1'b1, K1_In[15:0]}), .in_10({K2_In[16], 1'b1, K2_In[15:0]}),
    .in_11({K3_In[16], 1'b1, K3_In[15:0]}), .in_12(GPI_0), .in_13(GPI_1), .in_14(GPI_2), .in_15(GPI_3),
    .in_16(tnet_1_pc_do), .in_17(tnet_2_pc_do), .in_18(tnet_3_pc_do), .in_19(tnet_4_pc_do),
    .in_20({18{1'b0}}), .in_21({18{1'b0}}), .in_22({18{1'b0}}), .in_23({18{1'b0}}), .in_24({18{1'b0}}),
    .in_25({18{1'b0}}), .in_26({18{1'b0}}), .in_27({18{1'b0}}), .in_28({2'b11, counter_1_out[15:0]}),
    .in_29({2'b11, counter_1_out[31:16]}), .in_30({2'b11, RNG_r}), .in_31({18{1'b0}}), .out(multiplexer_1_out));
  assign GPO_2[15:0] = GPO_2[17] ? bootloader_machine_1_i_o_out : 16'bz;  // Driver driver_7
  PullDown #(.Bits(18)) pulldown_1 (.out(pulldown_1_out));
  assign pulldown_1_out = or_3_out ? multiplexer_1_out : 18'bz;  // Driver driver_8
  Bootloader_Machine bootloader_machine_1 (
    .Boot_Start(Power_On), .Pause(Pause_CPU), .Clock_In(Clock_Input), .Load_Din(OS_In),
    .I_O_In(pulldown_1_out[15:0]), .I_O_Reading(pulldown_1_out[16]), .I_O_Writing(pulldown_1_out[17]),
    .Int_Lines(rs_ff_1_q), .Int_Mask({4{bootloader_machine_1_lo_enabled[3]}}), .Hard_Reset(1'b0),
    .Running(Running), .Load_Adr(OS_Adr), .Kernel(bootloader_machine_1_kernel),
    .Reading_I_O(bootloader_machine_1_writing_i_o[0]), .I_O_Out(bootloader_machine_1_i_o_out),
    .Writing_I_O(bootloader_machine_1_writing_i_o[1]), .IOP(bootloader_machine_1_iop),
    .LO_Enabled(bootloader_machine_1_lo_enabled[3]));  // open: PC, HLB
  // Probe Full I/O Input on pulldown_1_out
  assign GPO_3[15:0] = GPO_3[17] ? bootloader_machine_1_i_o_out : 16'bz;  // Driver driver_9
  Delay delay_3 (.in(Running), .out(delay_3_out));
  PullDown #(.Bits(16)) pulldown_2 (.out(bootloader_machine_1_i_o_out));
  and and_3 (and_3_out, delay_3_out, ~Running);  // And
  or or_1 (or_1_out, bootloader_machine_1_writing_i_o[1], bootloader_machine_1_writing_i_o[0]);
  nor nor_1 (nor_1_out, bootloader_machine_1_iop[0], bootloader_machine_1_iop[1]);
  and and_4 (and_4_out, bootloader_machine_1_iop[3], bootloader_machine_1_iop[4]);
  Break CPU_HLT (.brk(and_3_out));
  and and_5 (rs_ff_1_q[2], or_1_out, ~or_3_out);  // And
  assign driver_10_out = or_3_out ? bootloader_machine_1_writing_i_o : 2'bz;  // Driver driver_10
  or or_2 (or_2_out, nor_1_out, and_4_out);
  or or_3 (or_3_out, ~or_2_out, bootloader_machine_1_kernel);  // Or
  Demultiplexer #(.Selector_Bits(5), .Bits(2)) demultiplexer_1 (
    .sel(bootloader_machine_1_iop), .in(driver_10_out), .out_0({D0_Out[32], demultiplexer_1_out_0[0]}),
    .out_1({D1_Out[32], demultiplexer_1_out_1[0]}), .out_2({D2_Out[32], demultiplexer_1_out_2[0]}),
    .out_3({D3_Out[32], demultiplexer_1_out_3[0]}), .out_4(demultiplexer_1_out_4),
    .out_5(demultiplexer_1_out_5), .out_6(demultiplexer_1_out_6), .out_7(demultiplexer_1_out_7),
    .out_8(TK0_Out[17:16]), .out_9(TK1_Out[17:16]), .out_10(TK2_Out[17:16]), .out_11(TK3_Out[17:16]),
    .out_12(GPO_0[17:16]), .out_13(GPO_1[17:16]), .out_14(GPO_2[17:16]), .out_15(GPO_3[17:16]),
    .out_16(demultiplexer_1_out_16), .out_17(demultiplexer_1_out_17), .out_18(demultiplexer_1_out_18),
    .out_19(demultiplexer_1_out_19), .out_28(demultiplexer_1_out_28), .out_29(demultiplexer_1_out_29),
    .out_30(demultiplexer_1_out_30), .out_31(demultiplexer_1_out_31));  // open: out_20, out_21, out_22, out_23, out_24, out_25, out_26, out_27
  PullDown #(.Bits(2)) pulldown_3 (.out(driver_10_out));
  RS_FF_AS rs_ff_as_5 (.S(demultiplexer_1_out_28[1]), .R(demultiplexer_1_out_29[1]), .Q(rs_ff_as_5_q));  // open: nQ
  and and_6 (and_6_out, Running, rs_ff_as_5_q);
  Counter #(.Bits(32)) counter_1 (.en(and_6_out), .C(Clock_Input), .clr(1'b0), .out(counter_1_out));  // open: ovf
  and and_7 (and_7_out, demultiplexer_1_out_30[1], ~Clock_Input);  // And
  Register #(.Bits(16)) PC_Status (
    .D(bootloader_machine_1_i_o_out), .C(Clock_Input), .en(demultiplexer_1_out_30[1]), .Q(Status_Code));
  PRNG #(.Bits(16)) RNG (.S(16'h55eb), .se(1'b0), .ne(1'b1), .C(Clock_Input), .R(RNG_r));
  Break Status_Update (.brk(delay_4_out));
  Delay #(.delayTime(2)) delay_4 (.in(and_7_out), .out(delay_4_out));
  // Probe Cycle Counter on counter_1_out
  or or_4 (or_4_out, demultiplexer_1_out_0[0], D0_Out[32]);
  or or_5 (or_5_out, demultiplexer_1_out_1[0], D1_Out[32]);
  or or_6 (or_6_out, demultiplexer_1_out_2[0], D2_Out[32]);
  or or_7 (or_7_out, demultiplexer_1_out_3[0], D3_Out[32]);
  assign D0_Out[31:16] = D0_Out[32] ? bootloader_machine_1_i_o_out : 16'bz;  // Driver driver_11
  TNET tnet_1 (
    .PC_Do(tnet_1_pc_do[15:0]), .PC_Ro(tnet_1_pc_do[16]), .PC_Wo(tnet_1_pc_do[17]),
    .PC_Di(bootloader_machine_1_i_o_out), .PC_Ri(demultiplexer_1_out_16[0]),
    .PC_Wi(demultiplexer_1_out_16[1]), .Clk_Outb(Clock_Input), .IO_Di(TNET_I_0[15:0]), .IO_Ri(TNET_I_0[16]),
    .IO_Wi(TNET_I_0[17]), .IO_Do(TNET_O_0[15:0]), .IO_Ro(TNET_O_0[16]), .IO_Wo(TNET_O_0[17]),
    .Clk_Inb(TNET_I_0[18]), .Ovr(TNET_I_0[19]));
  TNET tnet_2 (
    .PC_Do(tnet_2_pc_do[15:0]), .PC_Ro(tnet_2_pc_do[16]), .PC_Wo(tnet_2_pc_do[17]),
    .PC_Di(bootloader_machine_1_i_o_out), .PC_Ri(demultiplexer_1_out_17[0]),
    .PC_Wi(demultiplexer_1_out_17[1]), .Clk_Outb(Clock_Input), .IO_Di(TNET_I_1[15:0]), .IO_Ri(TNET_I_1[16]),
    .IO_Wi(TNET_I_1[17]), .IO_Do(TNET_O_1[15:0]), .IO_Ro(TNET_O_1[16]), .IO_Wo(TNET_O_1[17]),
    .Clk_Inb(TNET_I_1[18]), .Ovr(TNET_I_1[19]));
  TNET tnet_3 (
    .PC_Do(tnet_3_pc_do[15:0]), .PC_Ro(tnet_3_pc_do[16]), .PC_Wo(tnet_3_pc_do[17]),
    .PC_Di(bootloader_machine_1_i_o_out), .PC_Ri(demultiplexer_1_out_18[0]),
    .PC_Wi(demultiplexer_1_out_18[1]), .Clk_Outb(Clock_Input), .IO_Di(TNET_I_2[15:0]), .IO_Ri(TNET_I_2[16]),
    .IO_Wi(TNET_I_2[17]), .IO_Do(TNET_O_2[15:0]), .IO_Ro(TNET_O_2[16]), .IO_Wo(TNET_O_2[17]),
    .Clk_Inb(TNET_I_2[18]), .Ovr(TNET_I_2[19]));
  TNET tnet_4 (
    .PC_Do(tnet_4_pc_do[15:0]), .PC_Ro(tnet_4_pc_do[16]), .PC_Wo(tnet_4_pc_do[17]),
    .PC_Di(bootloader_machine_1_i_o_out), .PC_Ri(demultiplexer_1_out_19[0]),
    .PC_Wi(demultiplexer_1_out_19[1]), .Clk_Outb(Clock_Input), .IO_Di(TNET_I_3[15:0]), .IO_Ri(TNET_I_3[16]),
    .IO_Wi(TNET_I_3[17]), .IO_Do(TNET_O_3[15:0]), .IO_Ro(TNET_O_3[16]), .IO_Wo(TNET_O_3[17]),
    .Clk_Inb(TNET_I_3[18]), .Ovr(TNET_I_3[19]));
  CounterPreset #(.Bits(16)) D0_Adr (
    .en(or_4_out), .C(Clock_Input), .dir(1'b0), .in(bootloader_machine_1_i_o_out),
    .ld(demultiplexer_1_out_4[1]), .clr(1'b0), .out(D0_Out[15:0]));  // open: ovf
  assign D1_Out[31:16] = D1_Out[32] ? bootloader_machine_1_i_o_out : 16'bz;  // Driver driver_12
  CounterPreset #(.Bits(16)) D1_Adr (
    .en(or_5_out), .C(Clock_Input), .dir(1'b0), .in(bootloader_machine_1_i_o_out),
    .ld(demultiplexer_1_out_5[1]), .clr(1'b0), .out(D1_Out[15:0]));  // open: ovf
  assign D2_Out[31:16] = D2_Out[32] ? bootloader_machine_1_i_o_out : 16'bz;  // Driver driver_13
  CounterPreset #(.Bits(16)) D2_Adr (
    .en(or_6_out), .C(Clock_Input), .dir(1'b0), .in(bootloader_machine_1_i_o_out),
    .ld(demultiplexer_1_out_6[1]), .clr(1'b0), .out(D2_Out[15:0]));  // open: ovf
  assign D3_Out[31:16] = D3_Out[32] ? bootloader_machine_1_i_o_out : 16'bz;  // Driver driver_14
  CounterPreset #(.Bits(16)) D3_Adr (
    .en(or_7_out), .C(Clock_Input), .dir(1'b0), .in(bootloader_machine_1_i_o_out),
    .ld(demultiplexer_1_out_7[1]), .clr(1'b0), .out(D3_Out[15:0]));  // open: ovf

  assign D0_Out[33] = Clock_Input;
  assign D1_Out[33] = Clock_Input;
  assign D2_Out[33] = Clock_Input;
  assign D3_Out[33] = Clock_Input;
  assign GPO_0[18] = Clock_Input;
  assign GPO_1[18] = Clock_Input;
  assign GPO_2[18] = Clock_Input;
  assign GPO_3[18] = Clock_Input;
  assign TK0_Out[18] = Clock_Input;
  assign TK1_Out[18] = Clock_Input;
  assign TK2_Out[18] = Clock_Input;
  assign TK3_Out[18] = Clock_Input;
  assign TNET_O_0[19:18] = {1'b1, Clock_Input};
  assign TNET_O_1[19:18] = {1'b1, Clock_Input};
  assign TNET_O_2[19:18] = {1'b1, Clock_Input};
  assign TNET_O_3[19:18] = {1'b1, Clock_Input};

  // Notes on the sheet:
  //   Power_On: Initiates the boot process, or resumes execution if a halt has occurred.
  //   STOP: Stop the OS where it is. Like Pause, but at the OS level.
  //   Running: ON if the computer is running.
  //   D0_Out: Drive output
  //   0-15: Address
  //   16-31: Data
  //   32: Writing
  //   33: Clock
  //   D1_Out: Drive output
  //   0-15: Address
  //   16-31: Data
  //   32: Writing
  //   33: Clock
  //   D2_Out: Drive output
  //   0-15: Address
  //   16-31: Data
  //   32: Writing
  //   33: Clock
  //   D3_Out: Drive output
  //   0-15: Address
  //   16-31: Data
  //   32: Writing
  //   33: Clock
  //   Pause_CPU: Halts the CPU.
  //   GPI_0: General purpose input
  //   0-15: Data
  //   16: Read
  //   17: Write
  //   GPO_0: General purpose output
  //   0-15: Data
  //   16: Reading
  //   17: Writing
  //   18: Clock
  //   GPI_1: General purpose input
  //   0-15: Data
  //   16: Read
  //   17: Write
  //   GPO_1: General purpose output
  //   0-15: Data
  //   16: Reading
  //   17: Writing
  //   18: Clock
  //   GPI_2: General purpose input
  //   0-15: Data
  //   16: Read
  //   17: Write
  //   GPO_2: General purpose output
  //   0-15: Data
  //   16: Reading
  //   17: Writing
  //   18: Clock
  //   GPI_3: General purpose input
  //   0-15: Data
  //   16: Read
  //   17: Write
  //   GPO_3: General purpose output
  //   0-15: Data
  //   16: Reading
  //   17: Writing
  //   18: Clock
  //   TNET_O_0: TNET output
  //   0-15: Data
  //   16: Read
  //   17: Write
  //   18: Clock
  //   19: Constant 1
  //   TNET_I_0: TNET input
  //   0-15: Data
  //   16: Read
  //   17: Write
  //   18: Clock In
  //   19: Override inbound
  //   PAUS: Triggers the PAUS interrupt.
  //   TK0_Out: Terminal/Keyboard output
  //   0-15: Data out
  //   16: Reading keyboard
  //   17: Writing terminal
  //   18: Clock
  //   K0_In: Keyboard input
  //   0-15: Data in
  //   16: Buffer has char
  //   TK1_Out: Terminal/Keyboard output
  //   0-15: Data out
  //   16: Reading keyboard
  //   17: Writing terminal
  //   18: Clock
  //   TK2_Out: Terminal/Keyboard output
  //   0-15: Data out
  //   16: Reading keyboard
  //   17: Writing terminal
  //   18: Clock
  //   TK3_Out: Terminal/Keyboard output
  //   0-15: Data out
  //   16: Reading keyboard
  //   17: Writing terminal
  //   18: Clock
  //   K1_In: Keyboard input
  //   0-15: Data in
  //   16: Buffer has char
  //   K2_In: Keyboard input
  //   0-15: Data in
  //   16: Buffer has char
  //   K3_In: Keyboard input
  //   0-15: Data in
  //   16: Buffer has char
  //   TNET_O_1: TNET output
  //   0-15: Data
  //   16: Read
  //   17: Write
  //   18: Clock
  //   19: Constant 1
  //   TNET_I_1: TNET input
  //   0-15: Data
  //   16: Read
  //   17: Write
  //   18: Clock In
  //   19: Override inbound
  //   TNET_O_2: TNET output
  //   0-15: Data
  //   16: Read
  //   17: Write
  //   18: Clock
  //   19: Constant 1
  //   TNET_I_2: TNET input
  //   0-15: Data
  //   16: Read
  //   17: Write
  //   18: Clock In
  //   19: Override inbound
  //   TNET_O_3: TNET output
  //   0-15: Data
  //   16: Read
  //   17: Write
  //   18: Clock
  //   19: Constant 1
  //   TNET_I_3: TNET input
  //   0-15: Data
  //   16: Read
  //   17: Write
  //   18: Clock In
  //   19: Override inbound
  //   Terminal / Keyboard
  //   Interrupt Storage/Clearing
  //   General Purpose I/O
  //   0-15/16/17 Data/Read/Write
  //   TICK
  //   Internal Expansion
  //   Config
  //   Network Cards
  //   _________
  //   PVIO
  //   PVIO Detection
  //   Allowed IOP
  //   Kernel Only IOP
  //   1/0 Write/Read
  //   TCS Extra Features (Immutable 0-2)
  //   Getting TICK interrupt signal
  //   External Drive Controls
  //   D Rout
  //   D Dout
  //   D Wout
  //   A Dout
  //   A Wout
  //   TNET Configuration
  //   A Din
endmodule
